# Fritzing sketch kiln_controller (saved by Fritzing 0.9.3b)
breadboards: 1

parts:
  Raspberry_Pi_2 = Raspberry Pi 3 [part_number=RPI-3-V1.2]
  Part4 = Adafruit MAX31856 Thermocouple Amp [part_number="Adafruit #3263"]
  U2 = RELAY [package=relay-g5q]
  IC3 = MCP3008 8-channel 10-bit ADC [part_number=MCP3008]
  U3 = RELAY [package=relay-g5q]
  JP1 = Header 4 [package=screwterminal-3.5mm-4_lock]
  JP2 = Header 4 [package=screwterminal-3.5mm-4_lock]
  PS1 = prefix0000 [part_number=S-350-60]

nets:
  3V3: Raspberry_Pi_2.3V3, Part4.VIN
  N1: Raspberry_Pi_2.GIPO10, Part4.SDI
  N2: Raspberry_Pi_2.GIPO9, Part4.SDO
  N3: Raspberry_Pi_2.GIPO11, Part4.SCK
  GND: Raspberry_Pi_2.GND, Part4.GND, IC3.gnd, PS1.connector5
  N4: Raspberry_Pi_2.GIPO8, Part4.!CS
  N5: Raspberry_Pi_2.GIPO24, IC3.in_1
  N6: Raspberry_Pi_2.GIPO23, IC3.in_3
  N7: U2.COIL2, IC3.out_1
  N8: U2.MAIN, JP2.3
  N9: U2.NO, JP1.2
  N10: U2.COIL1, IC3.com, U3.COIL1, PS1.connector2
  N11: IC3.out_3, U3.COIL2
  N12: U3.MAIN, JP2.2, PS1.connector8
  N13: U3.NO, JP1.3
  N14: JP1.1, JP2.1, PS1.connector6
  N15: JP1.4, JP2.4, PS1.connector7

notes:
  220 VAC In
  220 VAC Out
  to kiln

custom parts:
  Adafruit MAX31856 Thermocouple Amp: Thermocouples are very sensitive, requiring a good amplifier with a cold-compensation reference, as well as calculations to handle any non-linearities. For a long time we've suggested our MAX31855K breakout, which works great but is only for K-type thermocouples. Now we're happy to offer a great new thermocouple amplifier/converter that can handle just about any type of thermocouple, and even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
